# Fritzing sketch Turret (saved by Fritzing 0.9.4)
circuit board: 12cm x 7cm
breadboards: 2

parts:
  Tilt_Servo = male pin header, 3 pins [form="♂ (male)"]
  LED_Reload = male pin header, 2 pins [form="♂ (male)"]
  LED_Firing = male pin header, 2 pins [form="♂ (male)"]
  LED_Mode = male pin header, 2 pins [form="♂ (male)"]
  LED_Reload_Resistor = Resistor [tolerance=±5% resistance=220 package=THT]
  LED_Mode_Resistor = Resistor [tolerance=±5% resistance=220 package=THT]
  MOSFET_Trigger_FQP30N06L = STP16NF06 N-Channel Power MOSFET [part_number=FQP30N06L]
  Diode = Rectifier Diode [part_number=1N4001 package="300 mil [THT]"]
  Gun_Trigger_(Blue) = male pin header, 3 pins [form="♂ (male)"]
  LED_Firing_Resistor = Resistor [tolerance=±5% resistance=220 package=THT]
  Pan_Servo = male pin header, 3 pins [form="♂ (male)"]
  Switch_Reload = male pin header, 2 pins [form="♂ (male)"]
  LED_USB = male pin header, 2 pins [form="♂ (male)"]
  LED_USB_Resistor = Resistor [tolerance=±5% resistance=220 package=THT]
  Trigger_220k = Resistor [tolerance=±5% resistance=220 package=THT]
  Trigger_10k = Resistor [tolerance=±5% resistance=10 package=THT]
  LED_Main_Power_Header = Arduino Uno (Rev3)
  Switch_Fire\_(Blue) = male pin header, 2 pins [form="♂ (male)"]
  Switch_Gun_Power = male pin header, 3 pins [form="♂ (male)"]
  LED_Gun_Power_(RES) = male pin header, 2 pins [form="♂ (male)"]
  Servo_Power_Jack = 2.1mm Barrel Jack with Terminal Block
  Gun_Power_Jack = 2.1mm Barrel Jack with Terminal Block
  Disable_Plate = male pin header, 2 pins [form="♂ (male)"]
  Disable_Plate_resistor = Resistor [tolerance=±5% resistance=1M package=THT]
  Switch_Manual_Fire = male pin header, 2 pins [form="♂ (male)"]
  Gun_Firing_Motor_(Grey) = Screw terminal - 2 pins [package=THT]
  Gun_main_motor_(R/G) = Screw terminal - 2 pins [package=THT]
  Switch_Servo_Power = male pin header, 2 pins [form="♂ (male)"]
  LED_Servo_Power_(RES) = male pin header, 2 pins [form="♂ (male)"]

nets:
  N1: Tilt_Servo.pin1, LED_Reload.pin2, LED_Firing.pin2, LED_Mode.pin2, MOSFET_Trigger_FQP30N06L.source, Pan_Servo.pin1, Switch_Reload.pin2, LED_USB.pin1, Trigger_10k.Pin_1, LED_Main_Power_Header.GND, LED_Gun_Power_(RES).pin1, Servo_Power_Jack.NEG, Gun_Power_Jack.NEG, Disable_Plate.pin2, Disable_Plate_resistor.Pin_1, Switch_Manual_Fire.pin1, Gun_Firing_Motor_(Grey).pin1, Gun_main_motor_(R/G).pin1, LED_Servo_Power_(RES).pin2
  N2: Tilt_Servo.pin2, Pan_Servo.pin2, Switch_Servo_Power.pin2, LED_Servo_Power_(RES).pin1
  N3: Tilt_Servo.pin3, LED_Main_Power_Header.D8
  N4: LED_Reload.pin1, LED_Reload_Resistor.Pin_1
  N5: LED_Firing.pin1, LED_Firing_Resistor.Pin_1
  N6: LED_Mode.pin1, LED_Mode_Resistor.Pin_1
  N7: LED_Reload_Resistor.Pin_0, LED_Main_Power_Header.D5_PWM
  N8: LED_Mode_Resistor.Pin_0, LED_Main_Power_Header.D4
  N9: MOSFET_Trigger_FQP30N06L.gate, Trigger_220k.Pin_1, Trigger_10k.Pin_0
  N10: MOSFET_Trigger_FQP30N06L.drain, Diode.anode, Switch_Manual_Fire.pin2, Gun_Firing_Motor_(Grey).pin2
  N11: Diode.cathode, Switch_Gun_Power.pin1, Gun_Power_Jack.POS
  N12: Gun_Trigger_(Blue).pin2, Switch_Fire\_(Blue).pin1
  N13: Gun_Trigger_(Blue).pin3, Switch_Fire\_(Blue).pin2
  N14: LED_Firing_Resistor.Pin_0, LED_Main_Power_Header.D2
  N15: Pan_Servo.pin3, LED_Main_Power_Header.D7
  N16: Switch_Reload.pin1, LED_Main_Power_Header.D10_PWM/SS
  N17: LED_USB.pin2, LED_USB_Resistor.Pin_1
  N18: LED_USB_Resistor.Pin_0, LED_Main_Power_Header.D3_PWM
  N19: Trigger_220k.Pin_0, LED_Main_Power_Header.D6_PWM
  N20: LED_Main_Power_Header.A0, Disable_Plate.pin1, Disable_Plate_resistor.Pin_0
  N21: Switch_Gun_Power.pin2, LED_Gun_Power_(RES).pin2, Gun_main_motor_(R/G).pin2
  N22: Servo_Power_Jack.POS, Switch_Servo_Power.pin1

notes:
  signal, x, ground
  Disable Plate header is A0
  Reload Switch is moved from pin 5 to 10.

custom parts:
  STP16NF06 N-Channel Power MOSFET: STP16NF06 N-channel Power MOSFET
